// Logisim project 32bic.circ as structural Verilog: 15 circuits, main circuit Terminal
module CPU (
  input  OVRD,
  input  [31:0] Din,
  output [15:0] DATA_ADDR,
  output [15:0] DATA_CHAN,
  output E_Dout,
  output [31:0] Dout,
  output L_Din
);

  wire clock_1_out, control_unit_1_a2d, control_unit_1_d2a, control_unit_1_e_dinc, control_unit_1_e_dout,
       control_unit_1_e_doutc, control_unit_1_e_mar, control_unit_1_e_par, control_unit_1_e_r0,
       control_unit_1_e_ram, control_unit_1_halt, control_unit_1_i_doutc, control_unit_1_i_mar,
       control_unit_1_i_par, control_unit_1_l_alu, control_unit_1_l_din, control_unit_1_l_mar,
       control_unit_1_l_r0, control_unit_1_p2a, control_unit_1_p2d, control_unit_1_par2a,
       control_unit_1_prom_pram, control_unit_1_reg_mode, control_unit_1_reset, control_unit_1_rw,
       controlled_buffer_1_out, keyboard_1_avail, not_1_out, not_2_out, not_3_out, or_1_out,
       pull_resistor_2_node;
  wire [1:0] alu_1_out_5;
  wire [3:0] control_unit_1_a, control_unit_1_alu_op, control_unit_1_b, control_unit_1_dr;
  wire [15:0] program_memory_1_a, ram_1_addr_out;
  wire [31:0] Din_t, or_2_out, program_memory_1_instruction, ram_1_data_out, ram_1_inst_dat,
       register_module_1_a_2, register_module_1_b_2;

  Clock clock_1 (.out(clock_1_out));
  or or_1 (or_1_out, OVRD, keyboard_1_avail);
  assign controlled_buffer_1_out = not_1_out ? clock_1_out : 1'bz;  // Controlled_Buffer controlled_buffer_1
  Pull_Resistor pull_resistor_1 (.node(controlled_buffer_1_out));
  not not_1 (not_1_out, pull_resistor_2_node);
  Pull_Resistor pull_resistor_2 (.node(pull_resistor_2_node));
  assign pull_resistor_2_node = not_2_out ? control_unit_1_halt : 1'bz;  // Controlled_Buffer controlled_buffer_2
  not not_2 (not_2_out, or_1_out);
  RAM ram_1 (
    .E_MAR(control_unit_1_e_mar), .ADDR_IN(ram_1_addr_out), .I_MAR(control_unit_1_i_mar),
    .CK(controlled_buffer_1_out), .CR(control_unit_1_reset), .ADDR_OUT(ram_1_addr_out),
    .L_MAR(control_unit_1_l_mar), .INST_ADDR(program_memory_1_a), .DATA_OUT(ram_1_data_out),
    .DATA_IN(ram_1_data_out), .R_W_IN(control_unit_1_rw), .E_RAM(control_unit_1_e_ram),
    .INST_DAT(ram_1_inst_dat), ._0_RAM__1_ROM(control_unit_1_prom_pram));
  Pull_Resistor pull_resistor_3 (.node(ram_1_addr_out));
  Program_Memory program_memory_1 (
    .E_PAR(control_unit_1_e_par), .Address(ram_1_addr_out), .I_PAR(control_unit_1_i_par),
    .P2A(control_unit_1_p2a), .Data(ram_1_data_out), .Address_2(ram_1_addr_out),
    .CK(controlled_buffer_1_out), .P2D(control_unit_1_p2d), .Instruction(program_memory_1_instruction),
    .A(program_memory_1_a), .D(ram_1_inst_dat), .RAM_0__ROM_1(control_unit_1_prom_pram),
    .PMR2A(control_unit_1_par2a));
  Bus_Control bus_control_1 (
    .out_5(ram_1_addr_out), .in_2(ram_1_addr_out), .in_1(ram_1_data_out), .out_6(ram_1_data_out),
    .A2D(control_unit_1_a2d), .D2A(control_unit_1_d2a));
  Pull_Resistor pull_resistor_4 (.node(ram_1_data_out));
  not not_3 (not_3_out, control_unit_1_prom_pram);
  assign ram_1_data_out = control_unit_1_l_r0 ? register_module_1_a_2 : 32'bz;  // Controlled_Buffer controlled_buffer_3
  Control_Unit control_unit_1 (
    .reg_mode(control_unit_1_reg_mode), .in_3(alu_1_out_5), .Clock(controlled_buffer_1_out),
    .DATA(program_memory_1_instruction), .HALT(control_unit_1_halt), .L_MAR(control_unit_1_l_mar),
    .I_MAR(control_unit_1_i_mar), .E_MAR(control_unit_1_e_mar), .E_RAM(control_unit_1_e_ram),
    .RW(control_unit_1_rw), .I_PAR(control_unit_1_i_par), .E_PAR(control_unit_1_e_par),
    .P2D(control_unit_1_p2d), .P2A(control_unit_1_p2a), .A2D(control_unit_1_a2d), .D2A(control_unit_1_d2a),
    .L_R0(control_unit_1_l_r0), .E_R0(control_unit_1_e_r0), .L_ALU(control_unit_1_l_alu),
    .E_DoutC(control_unit_1_e_doutc), .E_Dout(control_unit_1_e_dout), .E_DinC(control_unit_1_e_dinc),
    .L_Din(control_unit_1_l_din), .RESET(control_unit_1_reset), .dr(control_unit_1_dr), .A(control_unit_1_a),
    .B(control_unit_1_b), .alu_op(control_unit_1_alu_op), .PROM_PRAM(control_unit_1_prom_pram),
    .I_DoutC(control_unit_1_i_doutc), .PAR2A(control_unit_1_par2a));
  Pull_Resistor pull_resistor_5 (.node(Din));
  IO_Interface io_interface_1 (
    .L_Din(control_unit_1_l_din), .E_DinC(control_unit_1_e_dinc), .E_Dout(control_unit_1_e_dout),
    .E_DoutC(control_unit_1_e_doutc), .DoutC(DATA_ADDR), .Dout(Dout), .DinC(DATA_CHAN), .Din(or_2_out),
    .DATA(ram_1_data_out), .CK(controlled_buffer_1_out), .CR(control_unit_1_reset), .E_Dout_2(E_Dout),
    .L_Din_2(L_Din), .DATA_2(ram_1_data_out), .I_DoutC(control_unit_1_i_doutc));
  ALU alu_1 (
    .ALU_out(ram_1_data_out), .INS(control_unit_1_alu_op), .out_5(alu_1_out_5), .A(register_module_1_a_2),
    .B(register_module_1_b_2), .L_ALU(control_unit_1_l_alu));
  Register_Module register_module_1 (
    .Data(ram_1_data_out), .B_2(register_module_1_b_2), .A_2(register_module_1_a_2),
    .E_Reg_Write(control_unit_1_e_r0), .dr(control_unit_1_dr), .CK(controlled_buffer_1_out),
    .CR(control_unit_1_reset), .B(control_unit_1_b), .A(control_unit_1_a), .reg_mode(control_unit_1_reg_mode));
  assign or_2_out = Din | Din_t;  // OR_Gate or_2, 32 bits wide
  Pull_Resistor pull_resistor_6 (.node(Din_t));
  TTY #(.rows(5), .cols(40), .trigger("falling")) tty_1 (.data(Dout[6:0]), .clk(E_Dout));  // open: we, clr
  // Probe on ram_1_data_out
  Keyboard #(.trigger("falling")) keyboard_1 (
    .clk(L_Din), .avail(keyboard_1_avail), .data(Din_t[6:0]));  // open: re, clr
  LED ROM (.in(control_unit_1_prom_pram));
  LED RAM_2 (.in(not_3_out));

  // Other names for the same wires on the sheet: D[31:0] = Dout; ed = E_Dout; ld = L_Din

  // Notes on the sheet:
  //   32 Bit Integer Computer
  //   by Miles Smith
endmodule

// Arithmetic Unit
module ALU (
  input  [31:0] A,
  input  [31:0] B,
  input  [3:0] INS,
  input  L_ALU,
  output [1:0] out_5,
  output [31:0] ALU_out
);

  wire and_1_out, and_2_out, bitselector_1_out, comparator_1_eq, comparator_1_gt, comparator_1_lt;
  wire [1:0] controlled_buffer_2_out, controlled_buffer_3_out;
  wire [31:0] adder_1_out, and_3_out, bit_mask_1_out_3, controlled_buffer_4_out, divider_1_out,
       multiplexer_1_out, multiplier_1_out, not_1_out, or_2_out, random_1_out, subtractor_1_out, xor_1_out;

  Adder #(.width(32)) adder_1 (.a(A), .b(B), .out(adder_1_out));  // open: cin, cout
  Subtractor #(.width(32)) subtractor_1 (.a(A), .b(B), .out(subtractor_1_out));  // open: bin, bout
  Multiplier #(.width(32)) multiplier_1 (.a(A), .b(B), .out(multiplier_1_out));  // open: cin, cout
  Comparator #(.width(32)) comparator_1 (
    .a(A), .b(B), .gt(comparator_1_gt), .eq(comparator_1_eq), .lt(comparator_1_lt));
  Divider #(.width(32)) divider_1 (.a(A), .b(B), .out(divider_1_out));  // open: upper, rem
  and and_1 (and_1_out, comparator_1_gt, ~comparator_1_eq, ~comparator_1_lt);  // AND_Gate
  and and_2 (and_2_out, ~comparator_1_gt, ~comparator_1_eq, comparator_1_lt);  // AND_Gate
  Random #(.width(32)) random_1 (.clk(L_ALU), .out(random_1_out));  // open: next, clr
  Multiplexer #(.select(4), .width(32), .enable("false")) multiplexer_1 (
    .in0(adder_1_out), .in1(subtractor_1_out), .in2(multiplier_1_out), .in3(divider_1_out),
    .in4(random_1_out), .in5(and_3_out), .in6(or_2_out), .in7(xor_1_out), .in8(not_1_out),
    .in9(controlled_buffer_4_out), .in10(A), .in11(bit_mask_1_out_3), .out(multiplexer_1_out), .sel(INS));  // open: in12, in13, in14, in15
  assign ALU_out = L_ALU ? multiplexer_1_out : 32'bz;  // Controlled_Buffer controlled_buffer_1
  Pull_Resistor pull_resistor_1 (.node(L_ALU));
  assign controlled_buffer_2_out = and_1_out ? 2'b01 : 2'bz;  // Controlled_Buffer controlled_buffer_2
  Pull_Resistor pull_resistor_2 (.node(controlled_buffer_2_out));
  assign controlled_buffer_3_out = and_2_out ? 2'b10 : 2'bz;  // Controlled_Buffer controlled_buffer_3
  Pull_Resistor pull_resistor_3 (.node(controlled_buffer_3_out));
  assign and_3_out = A & B;  // AND_Gate and_3, 32 bits wide
  Pull_Resistor pull_resistor_4 (.node(multiplexer_1_out));
  assign out_5 = controlled_buffer_2_out | controlled_buffer_3_out;  // OR_Gate or_1, 2 bits wide
  assign or_2_out = A | B;  // OR_Gate or_2, 32 bits wide
  assign xor_1_out = A ^ B;  // XOR_Gate xor_1, 32 bits wide
  BitSelector #(.width(32)) bitselector_1 (.in(A), .out(bitselector_1_out), .sel(B[4:0]));
  assign not_1_out = ~A;  // NOT_Gate not_1, 32 bits wide
  assign controlled_buffer_4_out = bitselector_1_out ? 32'h1 : 32'bz;  // Controlled_Buffer controlled_buffer_4
  Pull_Resistor pull_resistor_5 (.node(controlled_buffer_4_out));
  Bit_Mask bit_mask_1 (.A(A[15:0]), .B(B[15:0]), .out_3(bit_mask_1_out_3[15:0]));
  Bit_Mask bit_mask_2 (.A(A[31:16]), .B(B[31:16]), .out_3(bit_mask_1_out_3[31:16]));

  // Notes on the sheet:
  //   0 ADD, 1 SUB, 2 MUL, 3 DIV, 4 AND, 5 OR, 6 XOR, 7 NOT, 8 BIT SELECT
endmodule

module Bit_Mask (
  input  [15:0] A,
  input  [15:0] B,
  output [15:0] out_3
);

  wire [15:0] not_1_out;

  Pull_Resistor pull_resistor_1 (.node(A));
  Pull_Resistor pull_resistor_2 (.node(B));
  assign not_1_out = ~B;  // NOT_Gate not_1, 16 bits wide
  assign out_3[0] = not_1_out[0] ? A[0] : 1'bz;  // Controlled_Buffer controlled_buffer_1
  assign out_3[1] = not_1_out[1] ? A[1] : 1'bz;  // Controlled_Buffer controlled_buffer_2
  assign out_3[2] = not_1_out[2] ? A[2] : 1'bz;  // Controlled_Buffer controlled_buffer_3
  assign out_3[3] = not_1_out[3] ? A[3] : 1'bz;  // Controlled_Buffer controlled_buffer_4
  assign out_3[4] = not_1_out[4] ? A[4] : 1'bz;  // Controlled_Buffer controlled_buffer_5
  assign out_3[5] = not_1_out[5] ? A[5] : 1'bz;  // Controlled_Buffer controlled_buffer_6
  assign out_3[6] = not_1_out[6] ? A[6] : 1'bz;  // Controlled_Buffer controlled_buffer_7
  assign out_3[7] = not_1_out[7] ? A[7] : 1'bz;  // Controlled_Buffer controlled_buffer_8
  assign out_3[8] = not_1_out[8] ? A[8] : 1'bz;  // Controlled_Buffer controlled_buffer_9
  assign out_3[9] = not_1_out[9] ? A[9] : 1'bz;  // Controlled_Buffer controlled_buffer_10
  assign out_3[10] = not_1_out[10] ? A[10] : 1'bz;  // Controlled_Buffer controlled_buffer_11
  assign out_3[11] = not_1_out[11] ? A[11] : 1'bz;  // Controlled_Buffer controlled_buffer_12
  assign out_3[12] = not_1_out[12] ? A[12] : 1'bz;  // Controlled_Buffer controlled_buffer_13
  assign out_3[13] = not_1_out[13] ? A[13] : 1'bz;  // Controlled_Buffer controlled_buffer_14
  assign out_3[14] = not_1_out[14] ? A[14] : 1'bz;  // Controlled_Buffer controlled_buffer_15
  assign out_3[15] = not_1_out[15] ? A[15] : 1'bz;  // Controlled_Buffer controlled_buffer_16
endmodule

// Register Unit
module Register_Module (
  input  CK,
  input  CR,
  input  [31:0] Data,
  input  [3:0] A,
  input  E_Reg_Write,
  input  [3:0] dr,
  input  reg_mode,
  input  [3:0] B,
  output [31:0] A_2,
  output [31:0] B_2
);

  wire decoder_1_out0, decoder_1_out1, decoder_1_out2, decoder_1_out3, decoder_1_out4, decoder_1_out5,
       decoder_1_out6, decoder_1_out7, decoder_1_out8, decoder_1_out9, decoder_1_out10, decoder_1_out11,
       decoder_1_out12, decoder_1_out13, decoder_1_out14, decoder_1_out15, not_1_out;
  wire [3:0] or_1_out, pull_resistor_1_node, pull_resistor_2_node;
  wire [31:0] register_1_q, register_2_q, register_3_q, register_4_q, register_5_q, register_6_q,
       register_7_q, register_8_q, register_9_q, register_10_q, register_11_q, register_12_q, register_13_q,
       register_14_q, register_15_q, register_16_q;

  Decoder #(.select(4), .disabled(0)) decoder_1 (
    .out0(decoder_1_out0), .out1(decoder_1_out1), .out2(decoder_1_out2), .out3(decoder_1_out3),
    .out4(decoder_1_out4), .out5(decoder_1_out5), .out6(decoder_1_out6), .out7(decoder_1_out7),
    .out8(decoder_1_out8), .out9(decoder_1_out9), .out10(decoder_1_out10), .out11(decoder_1_out11),
    .out12(decoder_1_out12), .out13(decoder_1_out13), .out14(decoder_1_out14), .out15(decoder_1_out15),
    .sel(or_1_out), .en(E_Reg_Write));
  assign or_1_out = pull_resistor_1_node | pull_resistor_2_node;  // OR_Gate or_1, 4 bits wide
  Pull_Resistor pull_resistor_1 (.node(pull_resistor_1_node));
  assign pull_resistor_1_node = not_1_out ? dr : 4'bz;  // Controlled_Buffer controlled_buffer_1
  not not_1 (not_1_out, reg_mode);
  Pull_Resistor pull_resistor_2 (.node(pull_resistor_2_node));
  assign pull_resistor_2_node = reg_mode ? A : 4'bz;  // Controlled_Buffer controlled_buffer_2
  Register #(.width(32)) register_1 (.D(Data), .en(decoder_1_out0), .Q(register_1_q), .clk(CK), .clr(CR));
  Register #(.width(32)) register_2 (.D(Data), .en(decoder_1_out1), .Q(register_2_q), .clk(CK), .clr(CR));
  Register #(.width(32)) register_3 (.D(Data), .en(decoder_1_out2), .Q(register_3_q), .clk(CK), .clr(CR));
  Register #(.width(32)) register_4 (.D(Data), .en(decoder_1_out3), .Q(register_4_q), .clk(CK), .clr(CR));
  Register #(.width(32)) register_5 (.D(Data), .en(decoder_1_out4), .Q(register_5_q), .clk(CK), .clr(CR));
  Register #(.width(32)) register_6 (.D(Data), .en(decoder_1_out5), .Q(register_6_q), .clk(CK), .clr(CR));
  Register #(.width(32)) register_7 (.D(Data), .en(decoder_1_out6), .Q(register_7_q), .clk(CK), .clr(CR));
  Register #(.width(32)) register_8 (.D(Data), .en(decoder_1_out7), .Q(register_8_q), .clk(CK), .clr(CR));
  Register #(.width(32)) register_9 (.D(Data), .en(decoder_1_out8), .Q(register_9_q), .clk(CK), .clr(CR));
  Register #(.width(32)) register_10 (.D(Data), .en(decoder_1_out9), .Q(register_10_q), .clk(CK), .clr(CR));
  Register #(.width(32)) register_11 (.D(Data), .en(decoder_1_out10), .Q(register_11_q), .clk(CK), .clr(CR));
  Register #(.width(32)) register_12 (.D(Data), .en(decoder_1_out11), .Q(register_12_q), .clk(CK), .clr(CR));
  Register #(.width(32)) register_13 (.D(Data), .en(decoder_1_out12), .Q(register_13_q), .clk(CK), .clr(CR));
  Register #(.width(32)) register_14 (.D(Data), .en(decoder_1_out13), .Q(register_14_q), .clk(CK), .clr(CR));
  Register #(.width(32)) register_15 (.D(Data), .en(decoder_1_out14), .Q(register_15_q), .clk(CK), .clr(CR));
  Register #(.width(32)) register_16 (.D(Data), .en(decoder_1_out15), .Q(register_16_q), .clk(CK), .clr(CR));
  Multiplexer #(.select(4), .width(32), .enable("false")) multiplexer_1 (
    .in0(register_1_q), .in1(register_2_q), .in2(register_3_q), .in3(register_4_q), .in4(register_5_q),
    .in5(register_6_q), .in6(register_7_q), .in7(register_8_q), .in8(register_9_q), .in9(register_10_q),
    .in10(register_11_q), .in11(register_12_q), .in12(register_13_q), .in13(register_14_q),
    .in14(register_15_q), .in15(register_16_q), .out(A_2), .sel(A));
  Multiplexer #(.select(4), .width(32), .enable("false")) multiplexer_2 (
    .in0(register_1_q), .in1(register_2_q), .in2(register_3_q), .in3(register_4_q), .in4(register_5_q),
    .in5(register_6_q), .in6(register_7_q), .in7(register_8_q), .in8(register_9_q), .in9(register_10_q),
    .in10(register_11_q), .in11(register_12_q), .in12(register_13_q), .in13(register_14_q),
    .in14(register_15_q), .in15(register_16_q), .out(B_2), .sel(B));
  Pull_Resistor pull_resistor_3 (.node(A_2));
  Pull_Resistor pull_resistor_4 (.node(B_2));

  // Notes on the sheet:
  //   4
  //   5
  //   6
  //   7
  //   8
  //   9
  //   A
  //   B
  //   C
  //   D
  //   E
  //   F
  //   I had to add this line to solve the problem with the DREG operand in address mode. It is now in the SREG A place in register mode
endmodule

// Control Sequencer
module Control_Unit (
  input  [31:0] DATA,
  input  Clock,
  input  [1:0] in_3,
  output L_MAR,
  output HALT,
  output I_MAR,
  output E_MAR,
  output E_RAM,
  output RW,
  output I_PAR,
  output E_PAR,
  output P2D,
  output P2A,
  output A2D,
  output D2A,
  output L_R0,
  output E_R0,
  output L_ALU,
  output E_DoutC,
  output E_Dout,
  output PROM_PRAM,
  output E_DinC,
  output L_Din,
  output RESET,
  output reg_mode,
  output I_DoutC,
  output [3:0] A,
  output [3:0] B,
  output [3:0] dr,
  output [3:0] alu_op,
  output PAR2A
);

  wire controlled_buffer_1_out, flag_decoder_1_e_par, flag_decoder_1_i_par;
  wire [3:0] Incrementor_q;
  wire [7:0] IR_q;
  wire [26:5] rom_1_data;

  Counter #(.width(4), .max('hf), .trigger("falling")) Incrementor (
    .Q(Incrementor_q), .clk(Clock), .clr(rom_1_data[22]));  // open: load, D, count, carry
  Register #(.trigger("falling")) IR (.D(DATA[7:0]), .en(rom_1_data[23]), .Q(IR_q), .clk(Clock), .clr(rom_1_data[22]));
  assign controlled_buffer_1_out = rom_1_data[25] ? Clock : 1'bz;  // Controlled_Buffer controlled_buffer_1
  Register #(.width(16)) register_1 (
    .D(DATA[23:8]), .en(rom_1_data[23]), .Q({alu_op, dr, B, A}), .clk(Clock));  // open: clr
  D_Flip_Flop d_ff_1 (.clk(controlled_buffer_1_out), .D(rom_1_data[26]), .Qn(PROM_PRAM));  // open: Q, preset, en, reset
  ROM #(.addrWidth(12), .dataWidth(29)) rom_1 (
    .addr({IR_q, Incrementor_q}),
    .data({PAR2A, I_DoutC, rom_1_data[26:25], L_MAR, rom_1_data[23:19], RESET, L_Din, E_DinC, E_Dout, E_DoutC, L_ALU, E_R0, L_R0, D2A, A2D, P2A, P2D, rom_1_data[6:5], RW, E_RAM, E_MAR, I_MAR, HALT}));  // open: sel
  or or_1 (I_PAR, flag_decoder_1_i_par, rom_1_data[5]);
  or or_2 (E_PAR, flag_decoder_1_e_par, rom_1_data[6]);
  Flag_Decoder flag_decoder_1 (
    .EPROM(rom_1_data[21:20]), .EN(rom_1_data[19]), .ALU(in_3), .I_PAR(flag_decoder_1_i_par),
    .E_PAR(flag_decoder_1_e_par));
  and and_1 (reg_mode, E_RAM, ~RW);  // AND_Gate

  // Notes on the sheet:
  //   DO NOT MODIFY
  //   UNLESS YOU KNOW WHAT YOU'RE DOING
  //   WHATEVER YOU DO...
  //   MicroCode ROM
  //   contents of rom_1 (hex, n*v repeats v):
  //   800000 20 400000 1278*0 104 1028 400000 13*0 104 838 400000 1 12*0 838 400000 14*0 1028 400000 14*0
  //   22 400000 14*0 26 400000 14*0 1001220 400000 14*0 c24 400000 14*0 10001220 400000 14*0 c40 400000
  //   14*0 2000140 400000 14*0 6000140 400000 14*0 2000c40 400000 14*0 6000c40 400000 46*0 1820 400000
  //   254*0 20 10a0 400000 13*0 21020 400000 14*0 8820 400000 14*0 20 80a0 400000 13*0 8320 400000 14*0
  //   10320 400000 14*0 4320 400000 14*0 8000020 400000 14*0 8004020 400000 396*0 1 0 40020 400000 238*0
  //   3020 400000 254*0 c40 400000 254*0 140 400000 14*0 80100 400000 14*0 280100 400000 14*0 180100
  //   400000 14*0 380100 400000 942*0 1 20 400000
endmodule

module IO_Interface (
  input  [31:0] Din,
  input  CK,
  input  CR,
  input  L_Din,
  input  E_DinC,
  input  E_Dout,
  input  I_DoutC,
  input  E_DoutC,
  input  [31:0] DATA,
  output [15:0] DoutC,
  output [15:0] DinC,
  output [31:0] Dout,
  output E_Dout_2,
  output L_Din_2,
  output [31:0] DATA_2
);

  Counter #(.width(16), .max('hffff)) counter_1 (
    .load(E_DoutC), .D(DATA[15:0]), .count(I_DoutC), .Q(DoutC), .clk(CK), .clr(CR));  // open: carry
  Pull_Resistor pull_resistor_1 (.node(E_Dout_2));
  assign E_Dout_2 = CK ? E_Dout : 1'bz;  // Controlled_Buffer controlled_buffer_1
  Register #(.width(32)) register_1 (.D(DATA), .en(E_Dout), .Q(Dout), .clk(CK), .clr(CR));
  Register #(.width(16)) register_2 (.D(DATA[15:0]), .en(E_DinC), .Q(DinC), .clk(CK), .clr(CR));
  Pull_Resistor pull_resistor_2 (.node(L_Din));
  Pull_Resistor pull_resistor_3 (.node(Din));
  assign DATA_2 = L_Din ? Din : 32'bz;  // Controlled_Buffer controlled_buffer_2

  assign L_Din_2 = L_Din;

  // Notes on the sheet:
  //   Out
  //   In
endmodule

// Random Access Memory
module RAM (
  input  E_MAR,
  input  [15:0] ADDR_IN,
  input  I_MAR,
  input  CK,
  input  CR,
  input  L_MAR,
  input  [15:0] INST_ADDR,
  input  [31:0] DATA_IN,
  input  R_W_IN,
  input  _0_RAM__1_ROM,
  input  E_RAM,
  output [31:0] DATA_OUT,
  output [15:0] ADDR_OUT,
  output [31:0] INST_DAT
);

  wire and_1_out, not_2_out, or_1_out, pull_resistor_1_node, xor_1_out;
  wire [15:0] MAR_q, multiplexer_1_out;
  wire [31:0] controlled_buffer_2_out, controlled_buffer_4_out, ram_1_data;

  Counter #(.width(16), .max('hffff)) MAR (
    .load(E_MAR), .D(ADDR_IN), .count(I_MAR), .Q(MAR_q), .clk(CK), .clr(CR));  // open: carry
  assign ADDR_OUT = L_MAR ? MAR_q : 16'bz;  // Controlled_Buffer controlled_buffer_1
  Multiplexer #(.width(16), .enable("false")) multiplexer_1 (
    .in0(MAR_q), .in1(INST_ADDR), .out(multiplexer_1_out), .sel(xor_1_out));
  xor xor_1 (xor_1_out, pull_resistor_1_node, and_1_out);
  and and_1 (and_1_out, pull_resistor_1_node, E_RAM);
  Pull_Resistor pull_resistor_1 (.node(pull_resistor_1_node));
  not not_1 (pull_resistor_1_node, _0_RAM__1_ROM);
  or or_1 (or_1_out, pull_resistor_1_node, E_RAM);
  RAM_part #(.addrWidth(16), .dataWidth(32), .bus("separate")) ram_1 (
    .addr(multiplexer_1_out), .din(controlled_buffer_2_out), .data(ram_1_data), .str(R_W_IN), .sel(or_1_out),
    .clk(CK), .ld(not_2_out), .clr(CR));
  assign controlled_buffer_2_out = R_W_IN ? DATA_IN : 32'bz;  // Controlled_Buffer controlled_buffer_2
  assign INST_DAT = pull_resistor_1_node ? ram_1_data : 32'bz;  // Controlled_Buffer controlled_buffer_3
  assign controlled_buffer_4_out = not_2_out ? ram_1_data : 32'bz;  // Controlled_Buffer controlled_buffer_4
  not not_2 (not_2_out, R_W_IN);
  assign DATA_OUT = E_RAM ? controlled_buffer_4_out : 32'bz;  // Controlled_Buffer controlled_buffer_5

  // Notes on the sheet:
  //   This unit looks cluttered because it was modified after the fact
  //   so the control unit could execute code from RAM
endmodule

// Program ROM
module Program_Memory (
  input  PMR2A,
  input  P2A,
  input  E_PAR,
  input  [15:0] Address,
  input  I_PAR,
  input  CK,
  input  P2D,
  input  RAM_0__ROM_1,
  input  [31:0] D,
  output [15:0] Address_2,
  output [31:0] Data,
  output [15:0] A,
  output [31:0] Instruction
);

  wire button_1_out, not_1_out;
  wire [31:0] rom_1_data;

  assign Address_2 = PMR2A ? A : 16'bz;  // Controlled_Buffer controlled_buffer_1
  Counter #(.width(16), .max('hffff)) counter_1 (
    .load(E_PAR), .D(Address), .count(I_PAR), .Q(A), .clk(CK), .clr(button_1_out));  // open: carry
  Button button_1 (.out(button_1_out));
  ROM #(.addrWidth(16), .dataWidth(32)) rom_1 (.addr(A), .data(rom_1_data), .sel(RAM_0__ROM_1));
  not not_1 (not_1_out, RAM_0__ROM_1);
  assign Address_2 = P2A ? Instruction[31:16] : 16'bz;  // Controlled_Buffer controlled_buffer_2
  Pull_Resistor pull_resistor_1 (.node(P2A));
  Multiplexer #(.width(32), .enable("false")) multiplexer_1 (
    .in0(rom_1_data), .in1(D), .out(Instruction), .sel(not_1_out));
  assign Data = P2D ? Instruction : 32'bz;  // Controlled_Buffer controlled_buffer_3
  Pull_Resistor pull_resistor_2 (.node(P2D));

  // Notes on the sheet:
  //   BIOS ROM
  //   contents of rom_1 (hex, n*v repeats v):
  //   690074 6e0074 690074 740074 690074 610074 740074 690074 6e0074 670074 200074 640074 610074 740074
  //   610074 200074 740074 790074 700074 650074 730074 2e0074 2e0074 2e0074 f0070 1b c0000c0 f0070 1e
  //   b5f00c0 200074 640074 6f0074 6e0074 650074 2e0074 a0074 690074 6d0074 700074 6f0074 720074 740074
  //   690074 6e0074 670074 200074 730074 680074 650074 6c0074 6c0074 200074 6c0074 650074 780074 690074
  //   630074 6f0074 6e0074 e0070 5 f0070 41 c5600c0 c9a0e51 e0070 72 f0070 47 b6300c0 c9a0e50 f0070 4b
  //   c5e00c0 e0070 75 f0070 50 b6300c0 c9a0e50 f0070 54 c5e00c0 e0070 6e f0070 59 b6300c0 c9a0e50 f0070
  //   5d c5e00c0 e0070 a f0070 62 b6300c0 c9a0e50 f0070 66 c5e00c0 2e0074 e0070 6 f0070 6c c5600c0 c9b0e51
  //   e0070 68 f0070 72 b6300c0 c9b0e50 f0070 76 c5e00c0 e0070 65 f0070 7b b6300c0 c9b0e50 f0070 7f
  //   c5e00c0 e0070 6c f0070 84 b6300c0 c9b0e50 f0070 88 c5e00c0 e0070 70 f0070 8d b6300c0 c9b0e50 f0070
  //   91 c5e00c0 e0070 a f0070 96 b6300c0 c9b0e50 f0070 9a c5e00c0 2e0074 e0070 6 f0070 a0 c5600c0 c9c0e51
  //   e0070 6c f0070 a6 b6300c0 c9c0e50 f0070 aa c5e00c0 e0070 69 f0070 af b6300c0 c9c0e50 f0070 b3
  //   c5e00c0 e0070 73 f0070 b8 b6300c0 c9c0e50 f0070 bc c5e00c0 e0070 74 f0070 c1 b6300c0 c9c0e50 f0070
  //   c5 c5e00c0 e0070 a f0070 ca b6300c0 c9c0e50 f0070 ce c5e00c0 2e0074 e0070 7 f0070 d4 c5600c0 c9d0e51
  //   e0070 63 f0070 da b6300c0 c9d0e50 f0070 de c5e00c0 e0070 6c f0070 e3 b6300c0 c9d0e50 f0070 e7
  //   c5e00c0 e0070 65 f0070 ec b6300c0 c9d0e50 f0070 f0 c5e00c0 e0070 61 f0070 f5 b6300c0 c9d0e50 f0070
  //   f9 c5e00c0 e0070 72 f0070 fe b6300c0 c9d0e50 f0070 102 c5e00c0 e0070 a f0070 107 b6300c0 c9d0e50
  //   f0070 10b c5e00c0 2e0074 e0070 6 f0070 111 c5600c0 c9e0e51 e0070 74 f0070 117 b6300c0 c9e0e50 f0070
  //   11b c5e00c0 e0070 65 f0070 120 b6300c0 c9e0e50 f0070 124 c5e00c0 e0070 78 f0070 129 b6300c0 c9e0e50
  //   f0070 12d c5e00c0 e0070 74 f0070 132 b6300c0 c9e0e50 f0070 136 c5e00c0 e0070 a f0070 13b b6300c0
  //   c9e0e50 f0070 13f c5e00c0 2e0074 e0070 7 f0070 145 c5600c0 c9f0e51 e0070 70 f0070 14b b6300c0
  //   c9f0e50 f0070 14f c5e00c0 e0070 6f f0070 154 b6300c0 c9f0e50 f0070 158 c5e00c0 e0070 72 f0070 15d
  //   b6300c0 c9f0e50 f0070 161 c5e00c0 e0070 74 f0070 166 b6300c0 c9f0e50 f0070 16a c5e00c0 e0070 73
  //   f0070 16f b6300c0 c9f0e50 f0070 173 c5e00c0 e0070 a f0070 178 b6300c0 c9f0e50 f0070 17c c5e00c0
  //   2e0074 e0070 6 f0070 182 c5600c0 ca00e51 e0070 65 f0070 188 b6300c0 ca00e50 f0070 18c c5e00c0 e0070
  //   78 f0070 191 b6300c0 ca00e50 f0070 195 c5e00c0 e0070 65 f0070 19a b6300c0 ca00e50 f0070 19e c5e00c0
  //   e0070 63 f0070 1a3 b6300c0 ca00e50 f0070 1a7 c5e00c0 e0070 a f0070 1ac b6300c0 ca00e50 f0070 1b0
  //   c5e00c0 2e0074 200074 640074 6f0074 6e0074 650074 2e0074 a0074 690074 6e0074 690074 740074 690074
  //   610074 740074 690074 6e0074 670074 200074 730074 680074 650074 6c0074 6c0074 2e0074 2e0074 2e0074
  //   e0070 f f0070 1d0 c5600c0 c980e51 e0070 f f0070 1d6 c5600c0 c990e51 200074 640074 6f0074 6e0074
  //   650074 2e0074 a0074 570074 650074 6c0074 630074 6f0074 6d0074 650074 200074 740074 6f0074 200074
  //   5a0074 610074 6e0074 690074 740074 610074 200074 4f0074 530074 2c0074 200074 620074 790074 200074
  //   4d0074 690074 6c0074 650074 730074 200074 530074 6d0074 690074 740074 680074 210074 a0074 a0074
  //   c980e50 f0070 209 c9500c0 c990e50 f0070 20d c9500c0 7a0074 6f0074 730074 3e0074 200074 a0070 20
  //   b0070 a c0070 60 ff d0071 d72 204cdc1 239bdc1 227adc1 e0d60 f0070 222 b6300c0 c980e50 f0070 226
  //   c5e00c0 21200c0 b0070 a c0070 60 ff d0071 d72 204cdc1 239bdc1 e0d60 f0070 234 b6300c0 c990e50 f0070
  //   238 c5e00c0 22700c0 e0070 a f0070 23e b6300c0 c980e50 f0070 242 c5e00c0 e0070 a f0070 247 b6300c0
  //   c990e50 f0070 24b c5e00c0 c980e50 f0070 24f b6300c0 c9d0e50 f0070 253 c7a00c0 10070 1 b381ec1
  //   c980e50 f0070 25a b6300c0 c9a0e50 f0070 25e c7a00c0 10070 1 34b1ec1 c980e50 f0070 265 b6300c0
  //   c9c0e50 f0070 269 c7a00c0 10070 1 b161ec1 c980e50 f0070 270 b6300c0 c9b0e50 f0070 274 c7a00c0 10070
  //   1 2991ec1 220074 c980e50 f0070 27c c6e00c0 220074 200074 790074 6f0074 750074 720074 650074 200074
  //   730074 740074 750074 700074 690074 640074 2e0074 200074 540074 720074 790074 200074 220074 680074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
endmodule

// Bus Ctrl
module Bus_Control (
  input  [31:0] in_1,
  input  [15:0] in_2,
  input  A2D,
  input  D2A,
  output [15:0] out_5,
  output [31:0] out_6
);

  assign out_5 = D2A ? in_1[15:0] : 16'bz;  // Controlled_Buffer controlled_buffer_1
  assign out_6[15:0] = A2D ? in_2 : 16'bz;  // Controlled_Buffer controlled_buffer_2
  Pull_Resistor pull_resistor_1 (.node(D2A));
  Pull_Resistor pull_resistor_2 (.node(A2D));
endmodule

// =
module Flag_Decoder (
  input  EN,
  input  [1:0] EPROM,
  input  [1:0] ALU,
  output I_PAR,
  output E_PAR
);

  wire and_1_out, and_2_out, and_3_out, and_4_out, decoder_1_out0, decoder_1_out1, decoder_1_out2,
       decoder_1_out3, decoder_2_out0, decoder_2_out1, decoder_2_out2, or_1_out;

  Decoder #(.select(2)) decoder_1 (
    .out0(decoder_1_out0), .out1(decoder_1_out1), .out2(decoder_1_out2), .out3(decoder_1_out3), .sel(EPROM));  // open: en
  Decoder #(.select(2)) decoder_2 (
    .out0(decoder_2_out0), .out1(decoder_2_out1), .out2(decoder_2_out2), .sel(ALU));  // open: out3, en
  and and_1 (and_1_out, decoder_1_out0, decoder_2_out0);
  and and_2 (and_2_out, decoder_1_out1, decoder_2_out1);
  and and_3 (and_3_out, decoder_1_out2, decoder_2_out2);
  and and_4 (and_4_out, decoder_1_out3, ~decoder_2_out0);  // AND_Gate
  assign I_PAR = EN ? ~or_1_out : 1'bz;  // Controlled_Inverter controlled_inverter_1
  or or_1 (or_1_out, and_1_out, and_2_out, and_3_out, and_4_out);
  Pull_Resistor pull_resistor_1 (.node(I_PAR));
  assign E_PAR = EN ? or_1_out : 1'bz;  // Controlled_Buffer controlled_buffer_1
  Pull_Resistor pull_resistor_2 (.node(E_PAR));
endmodule

module Terminal (
);

  wire button_1_out, cpu_1_e_dout, cpu_1_l_din, keyboard_1_avail, logic_board_1_clear_tty,
       logic_board_1_keyboard, logic_board_1_ovrd_out, logic_board_1_tty;
  wire [6:0] keyboard_1_data, logic_board_1_tty_data;
  wire [15:0] cpu_1_data_addr, cpu_1_data_chan, logic_board_1_external_rom_address,
       logic_board_1_external_rom_address_2;
  wire [31:0] cpu_1_dout, flash_rom_1_out_2, logic_board_1_to_din, zanita_os_rom_1_out_2;

  TTY #(.rows(14), .cols(47), .trigger("falling")) tty_1 (
    .data(logic_board_1_tty_data), .clk(logic_board_1_tty), .clr(logic_board_1_clear_tty));  // open: we
  CPU cpu_1 (
    .OVRD(logic_board_1_ovrd_out), .DATA_ADDR(cpu_1_data_addr), .E_Dout(cpu_1_e_dout), .Dout(cpu_1_dout),
    .DATA_CHAN(cpu_1_data_chan), .L_Din(cpu_1_l_din), .Din(logic_board_1_to_din));
  Keyboard #(.buflen(256), .trigger("falling")) keyboard_1 (
    .clk(logic_board_1_keyboard), .clr(button_1_out), .avail(keyboard_1_avail), .data(keyboard_1_data));  // open: re
  Button button_1 (.out(button_1_out));
  Logic_Board logic_board_1 (
    .External_ROM_Address(logic_board_1_external_rom_address), .DATA_IO_ADDR(cpu_1_data_addr),
    .DATA_IO_CHAN(cpu_1_data_chan), .E_DOUT(cpu_1_e_dout), .L_DIN(cpu_1_l_din), .TTY(logic_board_1_tty),
    .KEYBOARD(logic_board_1_keyboard), .TTY_Data(logic_board_1_tty_data), .Keyboard_Data(keyboard_1_data),
    .TO_Din(logic_board_1_to_din), .FROM_Dout(cpu_1_dout), .External_ROM_Data(zanita_os_rom_1_out_2),
    .ovrd_in(keyboard_1_avail), .ovrd_out(logic_board_1_ovrd_out), .Clear_TTY(logic_board_1_clear_tty),
    .External_ROM_Address_2(logic_board_1_external_rom_address_2), .External_ROM_Data_2(flash_rom_1_out_2));  // open: Enable, Load, TO_PORT_2
  Zanita_OS_ROM zanita_os_rom_1 (.out_2(zanita_os_rom_1_out_2), .in_1(logic_board_1_external_rom_address));
  Flash_ROM flash_rom_1 (.out_2(flash_rom_1_out_2), .in_1(logic_board_1_external_rom_address_2));
  Zanita_OS_ROM zanita_os_rom_2 ();  // open: out_2, in_1

  // Notes on the sheet:
  //   32 Bit Integer Computing System
endmodule

module Logic_Board (
  input  [15:0] DATA_IO_CHAN,
  input  E_DOUT,
  input  L_DIN,
  input  [6:0] Keyboard_Data,
  input  [31:0] FROM_Dout,
  input  [31:0] External_ROM_Data,
  input  [31:0] External_ROM_Data_2,
  input  [15:0] DATA_IO_ADDR,
  input  ovrd_in,
  output Clear_TTY,
  output [31:0] TO_Din,
  output [6:0] TTY_Data,
  output TTY,
  output KEYBOARD,
  output [31:0] TO_PORT_2,
  output [15:0] External_ROM_Address,
  output [15:0] External_ROM_Address_2,
  output Load,
  output Enable,
  output ovrd_out
);

  wire decoder_1_out0, decoder_1_out1, decoder_1_out2, decoder_1_out3, or_2_out;
  wire [0:0] demultiplexer_1_out0;
  wire [1:0] bit_extender_1_out, demultiplexer_1_out3;
  wire [31:7] controlled_buffer_4_out;

  Bit_Extender #(.in_width(16), .out_width(2)) bit_extender_1 (.in(DATA_IO_CHAN), .out(bit_extender_1_out));
  buf or_1 (KEYBOARD, demultiplexer_1_out0[0]);  // OR_Gate
  Demultiplexer #(.select(2), .width(2), .enable("false")) demultiplexer_1 (
    .out0({TTY, demultiplexer_1_out0[0]}), .out2({Enable, Load}), .out3(demultiplexer_1_out3),
    .in({E_DOUT, L_DIN}), .sel(bit_extender_1_out));  // open: out1
  Decoder #(.select(2), .enable("false")) decoder_1 (
    .out0(decoder_1_out0), .out1(decoder_1_out1), .out2(decoder_1_out2), .out3(decoder_1_out3),
    .sel(bit_extender_1_out));
  assign TO_Din[6:0] = or_2_out ? Keyboard_Data : 7'bz;  // Controlled_Buffer controlled_buffer_1
  buf or_2 (or_2_out, decoder_1_out0);  // OR_Gate
  assign TO_Din = decoder_1_out1 ? External_ROM_Data : 32'bz;  // Controlled_Buffer controlled_buffer_2
  assign TO_Din = decoder_1_out2 ? External_ROM_Data_2 : 32'bz;  // Controlled_Buffer controlled_buffer_3
  assign {controlled_buffer_4_out[31:16], Clear_TTY, controlled_buffer_4_out[14:7], TTY_Data} = decoder_1_out0 ? FROM_Dout : 32'bz;  // Controlled_Buffer controlled_buffer_4

  assign External_ROM_Address = DATA_IO_ADDR;
  assign External_ROM_Address_2 = DATA_IO_ADDR;
  assign ovrd_out = ovrd_in;
  assign TO_PORT_2 = FROM_Dout;

  // Notes on the sheet:
  //   Chn 0
  //   Motherboard Logic
  //   Chn 2, 3
  //   Chn 1
endmodule

module Flash_ROM (
  input  [15:0] in_1,
  output [31:0] out_2
);

  ROM #(.addrWidth(16), .dataWidth(32)) rom_1 (.addr(in_1), .data(out_2));  // open: sel

  // Notes on the sheet:
  //   contents of rom_1 (hex, n*v repeats v):
  //   b007c0de 4d 61 63 20 4f 53 20 58 a 100 5*0 11111111 22222222 33333333 44444444 55555555 66666666
  //   77777777 88888888 99999999 aaaaaaaa bbbbbbbb cccccccc dddddddd eeeeeeee ffffffff 11111111 22222222
  //   33333333 44444444 55555555 66666666 77777777 88888888 99999999 aaaaaaaa bbbbbbbb cccccccc dddddddd
  //   eeeeeeee ffffffff 11111111 22222222 33333333 44444444 55555555 66666666 77777777 88888888 99999999
  //   aaaaaaaa bbbbbbbb cccccccc dddddddd eeeeeeee ffffffff 11111111 22222222 33333333 44444444 55555555
  //   66666666 77777777 88888888 99999999 aaaaaaaa bbbbbbbb cccccccc dddddddd eeeeeeee ffffffff 11111111
  //   22222222 33333333 44444444 55555555 66666666 77777777 88888888 99999999 aaaaaaaa bbbbbbbb cccccccc
  //   dddddddd eeeeeeee ffffffff 11111111 22222222 33333333 44444444 55555555 66666666 77777777 88888888
  //   99999999 aaaaaaaa bbbbbbbb cccccccc dddddddd eeeeeeee ffffffff 11111111 22222222 33333333 44444444
  //   55555555 66666666 77777777 88888888 99999999 aaaaaaaa bbbbbbbb cccccccc dddddddd eeeeeeee ffffffff
  //   11111111 22222222 33333333 44444444 55555555 66666666 77777777 88888888 99999999 aaaaaaaa bbbbbbbb
  //   cccccccc dddddddd eeeeeeee ffffffff 11111111 22222222 33333333 44444444 55555555 66666666 77777777
  //   88888888 99999999 aaaaaaaa bbbbbbbb cccccccc dddddddd eeeeeeee ffffffff 11111111 22222222 33333333
  //   44444444 55555555 66666666 77777777 88888888 99999999 aaaaaaaa bbbbbbbb cccccccc dddddddd eeeeeeee
  //   ffffffff 11111111 22222222 33333333 44444444 55555555 66666666 77777777 88888888 99999999 aaaaaaaa
  //   bbbbbbbb cccccccc dddddddd eeeeeeee ffffffff 11111111 22222222 33333333 44444444 55555555 66666666
  //   77777777 88888888 99999999 aaaaaaaa bbbbbbbb cccccccc dddddddd eeeeeeee ffffffff 11111111 22222222
  //   33333333 44444444 55555555 66666666 77777777 88888888 99999999 aaaaaaaa bbbbbbbb cccccccc dddddddd
  //   eeeeeeee ffffffff 11111111 22222222 33333333 44444444 55555555 66666666 77777777 88888888 99999999
  //   aaaaaaaa bbbbbbbb cccccccc dddddddd eeeeeeee ffffffff 11111111 22222222 33333333 44444444 55555555
  //   66666666 77777777 88888888 99999999 aaaaaaaa bbbbbbbb cccccccc dddddddd eeeeeeee ffffffff 11111111
  //   22222222 33333333 44444444 55555555 66666666 77777777 88888888 99999999 aaaaaaaa bbbbbbbb cccccccc
  //   dddddddd eeeeeeee ffffffff
endmodule

module Zanita_OS_ROM (
  input  [15:0] in_1,
  output [31:0] out_2
);

  ROM #(.addrWidth(16), .dataWidth(32)) rom_1 (.addr(in_1), .data(out_2));  // open: sel

  // Notes on the sheet:
  //   contents of rom_1 (hex, n*v repeats v):
  //   b007c0de 5a 61 6e 69 74 61 20 4f 53 a b50 4*0 690074 6e0074 690074 740074 690074 610074 740074
  //   690074 6e0074 670074 200074 640074 610074 740074 610074 200074 740074 790074 700074 650074 730074
  //   2e0074 2e0074 2e0074 f0070 1b a8b00c0 f0070 1e 9ef00c0 200074 640074 6f0074 6e0074 650074 2e0074
  //   a0074 690074 6d0074 700074 6f0074 720074 740074 690074 6e0074 670074 200074 730074 680074 650074
  //   6c0074 6c0074 200074 6c0074 650074 780074 690074 630074 6f0074 6e0074 e0070 5 f0070 41 adf00c0
  //   b230e51 e0070 72 f0070 47 9f300c0 b230e50 f0070 4b ae700c0 e0070 75 f0070 50 9f300c0 b230e50 f0070
  //   54 ae700c0 e0070 6e f0070 59 9f300c0 b230e50 f0070 5d ae700c0 e0070 a f0070 62 9f300c0 b230e50 f0070
  //   66 ae700c0 2e0074 e0070 6 f0070 6c adf00c0 b240e51 e0070 68 f0070 72 9f300c0 b240e50 f0070 76
  //   ae700c0 e0070 65 f0070 7b 9f300c0 b240e50 f0070 7f ae700c0 e0070 6c f0070 84 9f300c0 b240e50 f0070
  //   88 ae700c0 e0070 70 f0070 8d 9f300c0 b240e50 f0070 91 ae700c0 e0070 a f0070 96 9f300c0 b240e50 f0070
  //   9a ae700c0 2e0074 e0070 6 f0070 a0 adf00c0 b250e51 e0070 6c f0070 a6 9f300c0 b250e50 f0070 aa
  //   ae700c0 e0070 69 f0070 af 9f300c0 b250e50 f0070 b3 ae700c0 e0070 73 f0070 b8 9f300c0 b250e50 f0070
  //   bc ae700c0 e0070 74 f0070 c1 9f300c0 b250e50 f0070 c5 ae700c0 e0070 a f0070 ca 9f300c0 b250e50 f0070
  //   ce ae700c0 2e0074 e0070 7 f0070 d4 adf00c0 b260e51 e0070 63 f0070 da 9f300c0 b260e50 f0070 de
  //   ae700c0 e0070 6c f0070 e3 9f300c0 b260e50 f0070 e7 ae700c0 e0070 65 f0070 ec 9f300c0 b260e50 f0070
  //   f0 ae700c0 e0070 61 f0070 f5 9f300c0 b260e50 f0070 f9 ae700c0 e0070 72 f0070 fe 9f300c0 b260e50
  //   f0070 102 ae700c0 e0070 a f0070 107 9f300c0 b260e50 f0070 10b ae700c0 2e0074 e0070 6 f0070 111
  //   adf00c0 b270e51 e0070 74 f0070 117 9f300c0 b270e50 f0070 11b ae700c0 e0070 65 f0070 120 9f300c0
  //   b270e50 f0070 124 ae700c0 e0070 78 f0070 129 9f300c0 b270e50 f0070 12d ae700c0 e0070 74 f0070 132
  //   9f300c0 b270e50 f0070 136 ae700c0 e0070 a f0070 13b 9f300c0 b270e50 f0070 13f ae700c0 2e0074 e0070 7
  //   f0070 145 adf00c0 b280e51 e0070 70 f0070 14b 9f300c0 b280e50 f0070 14f ae700c0 e0070 6f f0070 154
  //   9f300c0 b280e50 f0070 158 ae700c0 e0070 72 f0070 15d 9f300c0 b280e50 f0070 161 ae700c0 e0070 74
  //   f0070 166 9f300c0 b280e50 f0070 16a ae700c0 e0070 73 f0070 16f 9f300c0 b280e50 f0070 173 ae700c0
  //   e0070 a f0070 178 9f300c0 b280e50 f0070 17c ae700c0 2e0074 e0070 6 f0070 182 adf00c0 b290e51 e0070
  //   65 f0070 188 9f300c0 b290e50 f0070 18c ae700c0 e0070 78 f0070 191 9f300c0 b290e50 f0070 195 ae700c0
  //   e0070 65 f0070 19a 9f300c0 b290e50 f0070 19e ae700c0 e0070 63 f0070 1a3 9f300c0 b290e50 f0070 1a7
  //   ae700c0 e0070 a f0070 1ac 9f300c0 b290e50 f0070 1b0 ae700c0 2e0074 200074 640074 6f0074 6e0074
  //   650074 2e0074 a0074 690074 6e0074 690074 740074 690074 610074 740074 690074 6e0074 670074 200074
  //   730074 680074 650074 6c0074 6c0074 2e0074 2e0074 2e0074 e0070 f f0070 1d0 adf00c0 b210e51 e0070 f
  //   f0070 1d6 adf00c0 b220e51 200074 640074 6f0074 6e0074 650074 2e0074 a0074 570074 650074 6c0074
  //   630074 6f0074 6d0074 650074 200074 740074 6f0074 200074 5a0074 610074 6e0074 690074 740074 610074
  //   200074 4f0074 530074 2c0074 200074 620074 790074 200074 4d0074 690074 6c0074 650074 730074 200074
  //   530074 6d0074 690074 740074 680074 210074 a0074 a0074 b210e50 f0070 209 b1e00c0 b220e50 f0070 20d
  //   b1e00c0 7a0074 6f0074 730074 3e0074 200074 a0070 20 b0070 a c0070 60 ff d0071 d72 204cdc1 239bdc1
  //   227adc1 e0d60 f0070 222 9f300c0 b210e50 f0070 226 ae700c0 21200c0 b0070 a c0070 60 ff d0071 d72
  //   204cdc1 239bdc1 e0d60 f0070 234 9f300c0 b220e50 f0070 238 ae700c0 22700c0 e0070 a f0070 23e 9f300c0
  //   b210e50 f0070 242 ae700c0 e0070 a f0070 247 9f300c0 b220e50 f0070 24b ae700c0 b210e50 f0070 24f
  //   9f300c0 b260e50 f0070 253 b0300c0 10070 1 9cd1ec1 b210e50 f0070 25a 9f300c0 b230e50 f0070 25e
  //   b0300c0 10070 1 34d1ec1 b210e50 f0070 265 9f300c0 b250e50 f0070 269 b0300c0 10070 1 9ab1ec1 b210e50
  //   f0070 270 9f300c0 b240e50 f0070 274 b0300c0 10070 1 29b1ec1 220074 b210e50 f0070 27c af700c0 220074
  //   200074 6e0074 6f0074 740074 200074 720074 650074 630074 6f0074 670074 6e0074 690074 7a0074 650074 64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
endmodule

module Disp_Driver (
  input  [31:0] in_1,
  input  in_2,
  output [31:0] out_3,
  output [31:0] out_4,
  output [31:0] out_5,
  output [31:0] out_6,
  output [31:0] out_7,
  output [31:0] out_8,
  output [31:0] out_9,
  output [31:0] out_10,
  output [31:0] out_11,
  output [31:0] out_12,
  output [31:0] out_13,
  output [31:0] out_14,
  output [31:0] out_15,
  output [31:0] out_16,
  output [31:0] out_17,
  output [31:0] out_18,
  output [31:0] out_19,
  output [31:0] out_20,
  output [31:0] out_21,
  output [31:0] out_22,
  output [31:0] out_23,
  output [31:0] out_24,
  output [31:0] out_25,
  output [31:0] out_26,
  output [31:0] out_27,
  output [31:0] out_28,
  output [31:0] out_29,
  output [31:0] out_30,
  output [31:0] out_31,
  output [31:0] out_32,
  output [31:0] out_33,
  output [31:0] out_34
);

  wire comparator_1_eq;
  wire [4:0] counter_1_q;
  wire [31:0] shift_register_1_q0, shift_register_1_q1, shift_register_1_q2, shift_register_1_q3,
       shift_register_1_q4, shift_register_1_q5, shift_register_1_q6, shift_register_1_q7,
       shift_register_1_q8, shift_register_1_q9, shift_register_1_q10, shift_register_1_q11,
       shift_register_1_q12, shift_register_1_q13, shift_register_1_q14, shift_register_1_q15,
       shift_register_1_q16, shift_register_1_q17, shift_register_1_q18, shift_register_1_q19,
       shift_register_1_q20, shift_register_1_q21, shift_register_1_q22, shift_register_1_q23,
       shift_register_1_q24, shift_register_1_q25, shift_register_1_q26, shift_register_1_q27,
       shift_register_1_q28, shift_register_1_q29, shift_register_1_q30, shift_register_1_q31;

  Counter #(.width(5), .max('h1f), .trigger("falling")) counter_1 (
    .Q(counter_1_q), .clk(in_2));  // open: load, D, count, carry, clr
  Shift_Register #(.width(32), .length(32), .trigger("falling")) shift_register_1 (
    .in(in_1), .clk(in_2), .q0(shift_register_1_q0), .q1(shift_register_1_q1), .q2(shift_register_1_q2),
    .q3(shift_register_1_q3), .q4(shift_register_1_q4), .q5(shift_register_1_q5), .q6(shift_register_1_q6),
    .q7(shift_register_1_q7), .q8(shift_register_1_q8), .q9(shift_register_1_q9), .q10(shift_register_1_q10),
    .q11(shift_register_1_q11), .q12(shift_register_1_q12), .q13(shift_register_1_q13),
    .q14(shift_register_1_q14), .q15(shift_register_1_q15), .q16(shift_register_1_q16),
    .q17(shift_register_1_q17), .q18(shift_register_1_q18), .q19(shift_register_1_q19),
    .q20(shift_register_1_q20), .q21(shift_register_1_q21), .q22(shift_register_1_q22),
    .q23(shift_register_1_q23), .q24(shift_register_1_q24), .q25(shift_register_1_q25),
    .q26(shift_register_1_q26), .q27(shift_register_1_q27), .q28(shift_register_1_q28),
    .q29(shift_register_1_q29), .q30(shift_register_1_q30), .q31(shift_register_1_q31));  // open: shift, out, load, clr, d0, d1, d2, d3, d4, d5, d6, d7, d8, d9, d10, d11, d12, d13, d14, d15, d16, d17, d18, d19, d20, d21, d22, d23, d24, d25, d26, d27, d28, d29, d30, d31
  Comparator #(.width(5)) comparator_1 (.a(counter_1_q), .b({5{1'b0}}), .eq(comparator_1_eq));  // open: gt, lt
  Shift_Register #(.width(32), .length(32)) shift_register_2 (
    .clk(comparator_1_eq), .load(comparator_1_eq), .d0(shift_register_1_q0), .q0(out_3),
    .d1(shift_register_1_q1), .q1(out_4), .d2(shift_register_1_q2), .q2(out_5), .d3(shift_register_1_q3),
    .q3(out_6), .d4(shift_register_1_q4), .q4(out_7), .d5(shift_register_1_q5), .q5(out_8),
    .d6(shift_register_1_q6), .q6(out_9), .d7(shift_register_1_q7), .q7(out_10), .d8(shift_register_1_q8),
    .q8(out_11), .d9(shift_register_1_q9), .q9(out_12), .d10(shift_register_1_q10), .q10(out_13),
    .d11(shift_register_1_q11), .q11(out_14), .d12(shift_register_1_q12), .q12(out_15),
    .d13(shift_register_1_q13), .q13(out_16), .d14(shift_register_1_q14), .q14(out_17),
    .d15(shift_register_1_q15), .q15(out_18), .d16(shift_register_1_q16), .q16(out_19),
    .d17(shift_register_1_q17), .q17(out_20), .d18(shift_register_1_q18), .q18(out_21),
    .d19(shift_register_1_q19), .q19(out_22), .d20(shift_register_1_q20), .q20(out_23),
    .d21(shift_register_1_q21), .q21(out_24), .d22(shift_register_1_q22), .q22(out_25),
    .d23(shift_register_1_q23), .q23(out_26), .d24(shift_register_1_q24), .q24(out_27),
    .d25(shift_register_1_q25), .q25(out_28), .d26(shift_register_1_q26), .q26(out_29),
    .d27(shift_register_1_q27), .q27(out_30), .d28(shift_register_1_q28), .q28(out_31),
    .d29(shift_register_1_q29), .q29(out_32), .d30(shift_register_1_q30), .q30(out_33),
    .d31(shift_register_1_q31), .q31(out_34));  // open: shift, in, out, clr
endmodule
